// Logisim project rv32_logisim_cpu.circ as structural Verilog: 9 circuits, main circuit main
module main (
);

  wire button_1_out, clock_1_out, cpu_1_illegal, cpu_1_load, cpu_1_store, or_1_out;
  wire [2:0] cpu_1_memwidth;
  wire [31:0] cpu_1_memaddr, cpu_1_pc, cpu_1_storevalue, memory_1_loadvalue, ProgramROM_data;

  Clock clock_1 (.out(clock_1_out));
  Button button_1 (.out(button_1_out));
  or or_1 (or_1_out, cpu_1_illegal, clock_1_out);
  CPU cpu_1 (
    .Instruction(ProgramROM_data), .LoadValue(memory_1_loadvalue), .Clock(or_1_out), .Reset(button_1_out),
    .Illegal(cpu_1_illegal), .MemWidth(cpu_1_memwidth), .Store(cpu_1_store), .Load(cpu_1_load),
    .MemAddr(cpu_1_memaddr), .StoreValue(cpu_1_storevalue), .PC(cpu_1_pc));
  ROM #(.addrWidth(24), .dataWidth(32)) ProgramROM (.addr(cpu_1_pc[25:2]), .data(ProgramROM_data));
  Memory memory_1 (
    .Address(cpu_1_memaddr), .Store(cpu_1_store), .Load(cpu_1_load), .Width(cpu_1_memwidth),
    .StoreValue(cpu_1_storevalue), .Clock(or_1_out), .LoadValue(memory_1_loadvalue));

  // Notes on the sheet:
  //   contents of ProgramROM (hex, n*v repeats v):
  //   8137 81b7 3c000ef 100073 2a05463 593 100613 58693 fff50513 c585b3 68613 fe0518e3 58513 8067 100593
  //   58513 8067 ff010113 112623 1400513 97 fc0080e7 c12083 1010113 8067
endmodule

module Extractor (
  input  [31:0] Instruction,
  input  [2:0] Format,
  output [6:0] Opcode,
  output [4:0] RD,
  output [2:0] Funct3,
  output [4:0] RS1,
  output [4:0] RS2,
  output Bit30,
  output [31:0] Immediate
);

  Multiplexer #(.select(3), .width(32)) multiplexer_1 (
    .in1({{21{Instruction[31]}}, Instruction[30:20]}),
    .in2({{21{Instruction[31]}}, Instruction[30:25], Instruction[11:7]}),
    .in3({{20{Instruction[31]}}, Instruction[30], Instruction[7], Instruction[29:25], Instruction[11:8], 1'b0}),
    .in4({Instruction[31:12], {12{1'b0}}}),
    .in5({{12{Instruction[31]}}, Instruction[19:12], Instruction[20], Instruction[30:21], 1'b0}),
    .in6({32{1'b0}}), .in7({32{1'b0}}), .out(Immediate), .sel(Format));  // open: in0

  assign Bit30 = Instruction[30];
  assign Funct3 = Instruction[14:12];
  assign Opcode = Instruction[6:0];
  assign RD = Instruction[11:7];
  assign RS1 = Instruction[19:15];
  assign RS2 = Instruction[24:20];

  // Notes on the sheet:
  //   I-type
  //   S-type
  //   B-type
  //   U-type
  //   J-type
endmodule

module Registers16 (
  input  Write,
  input  [3:0] RD,
  input  Clock,
  input  [31:0] Data,
  input  [3:0] RS1,
  input  [3:0] RS2,
  output [31:0] Out1,
  output [31:0] Out2
);

  wire decoder_1_out0, decoder_1_out1, decoder_1_out2, decoder_1_out3, decoder_1_out4, decoder_1_out5,
       decoder_1_out6, decoder_1_out7, decoder_1_out8, decoder_1_out9, decoder_1_out10, decoder_1_out11,
       decoder_1_out12, decoder_1_out13, decoder_1_out14, decoder_1_out15;
  wire [31:0] register_1_q, register_2_q, register_3_q, register_4_q, register_5_q, register_6_q,
       register_7_q, register_8_q, register_9_q, register_10_q, register_11_q, register_12_q, register_13_q,
       register_14_q, register_15_q, register_16_q;

  Multiplexer #(.select(4), .width(32)) multiplexer_1 (
    .in0(register_1_q), .in1(register_2_q), .in2(register_3_q), .in3(register_4_q), .in4(register_5_q),
    .in5(register_6_q), .in6(register_7_q), .in7(register_8_q), .in8(register_9_q), .in9(register_10_q),
    .in10(register_11_q), .in11(register_12_q), .in12(register_13_q), .in13(register_14_q),
    .in14(register_15_q), .in15(register_16_q), .out(Out1), .sel(RS1));
  Multiplexer #(.select(4), .width(32)) multiplexer_2 (
    .in0(register_1_q), .in1(register_2_q), .in2(register_3_q), .in3(register_4_q), .in4(register_5_q),
    .in5(register_6_q), .in6(register_7_q), .in7(register_8_q), .in8(register_9_q), .in9(register_10_q),
    .in10(register_11_q), .in11(register_12_q), .in12(register_13_q), .in13(register_14_q),
    .in14(register_15_q), .in15(register_16_q), .out(Out2), .sel(RS2));
  Decoder #(.select(4)) decoder_1 (
    .out0(decoder_1_out0), .out1(decoder_1_out1), .out2(decoder_1_out2), .out3(decoder_1_out3),
    .out4(decoder_1_out4), .out5(decoder_1_out5), .out6(decoder_1_out6), .out7(decoder_1_out7),
    .out8(decoder_1_out8), .out9(decoder_1_out9), .out10(decoder_1_out10), .out11(decoder_1_out11),
    .out12(decoder_1_out12), .out13(decoder_1_out13), .out14(decoder_1_out14), .out15(decoder_1_out15),
    .sel(RD), .en(Write));
  Register #(.trigger("falling"), .width(32)) register_1 (
    .D(Data), .en(decoder_1_out0), .clk(Clock), .Q(register_1_q));  // open: clr
  Register #(.trigger("falling"), .width(32)) register_2 (
    .D(Data), .en(decoder_1_out1), .clk(Clock), .Q(register_2_q));  // open: clr
  Register #(.trigger("falling"), .width(32)) register_3 (
    .D(Data), .en(decoder_1_out2), .clk(Clock), .Q(register_3_q));  // open: clr
  Register #(.trigger("falling"), .width(32)) register_4 (
    .D(Data), .en(decoder_1_out3), .clk(Clock), .Q(register_4_q));  // open: clr
  Register #(.trigger("falling"), .width(32)) register_5 (
    .D(Data), .en(decoder_1_out4), .clk(Clock), .Q(register_5_q));  // open: clr
  Register #(.trigger("falling"), .width(32)) register_6 (
    .D(Data), .en(decoder_1_out5), .clk(Clock), .Q(register_6_q));  // open: clr
  Register #(.trigger("falling"), .width(32)) register_7 (
    .D(Data), .en(decoder_1_out6), .clk(Clock), .Q(register_7_q));  // open: clr
  Register #(.trigger("falling"), .width(32)) register_8 (
    .D(Data), .en(decoder_1_out7), .clk(Clock), .Q(register_8_q));  // open: clr
  Register #(.trigger("falling"), .width(32)) register_9 (
    .D(Data), .en(decoder_1_out8), .clk(Clock), .Q(register_9_q));  // open: clr
  Register #(.trigger("falling"), .width(32)) register_10 (
    .D(Data), .en(decoder_1_out9), .clk(Clock), .Q(register_10_q));  // open: clr
  Register #(.trigger("falling"), .width(32)) register_11 (
    .D(Data), .en(decoder_1_out10), .clk(Clock), .Q(register_11_q));  // open: clr
  Register #(.trigger("falling"), .width(32)) register_12 (
    .D(Data), .en(decoder_1_out11), .clk(Clock), .Q(register_12_q));  // open: clr
  Register #(.trigger("falling"), .width(32)) register_13 (
    .D(Data), .en(decoder_1_out12), .clk(Clock), .Q(register_13_q));  // open: clr
  Register #(.trigger("falling"), .width(32)) register_14 (
    .D(Data), .en(decoder_1_out13), .clk(Clock), .Q(register_14_q));  // open: clr
  Register #(.trigger("falling"), .width(32)) register_15 (
    .D(Data), .en(decoder_1_out14), .clk(Clock), .Q(register_15_q));  // open: clr
  Register #(.trigger("falling"), .width(32)) register_16 (
    .D(Data), .en(decoder_1_out15), .clk(Clock), .Q(register_16_q));  // open: clr
endmodule

module Registers16WithZero (
  input  Write,
  input  [3:0] RD,
  input  Clock,
  input  [31:0] Data,
  input  [3:0] RS1,
  input  [3:0] RS2,
  output [31:0] Out1,
  output [31:0] Out2
);

  wire decoder_1_out1, decoder_1_out2, decoder_1_out3, decoder_1_out4, decoder_1_out5, decoder_1_out6,
       decoder_1_out7, decoder_1_out8, decoder_1_out9, decoder_1_out10, decoder_1_out11, decoder_1_out12,
       decoder_1_out13, decoder_1_out14, decoder_1_out15;
  wire [31:0] register_1_q, register_2_q, register_3_q, register_4_q, register_5_q, register_6_q,
       register_7_q, register_8_q, register_9_q, register_10_q, register_11_q, register_12_q, register_13_q,
       register_14_q, register_15_q;

  Multiplexer #(.select(4), .width(32)) multiplexer_1 (
    .in0({32{1'b0}}), .in1(register_1_q), .in2(register_2_q), .in3(register_3_q), .in4(register_4_q),
    .in5(register_5_q), .in6(register_6_q), .in7(register_7_q), .in8(register_8_q), .in9(register_9_q),
    .in10(register_10_q), .in11(register_11_q), .in12(register_12_q), .in13(register_13_q),
    .in14(register_14_q), .in15(register_15_q), .out(Out1), .sel(RS1));
  Multiplexer #(.select(4), .width(32)) multiplexer_2 (
    .in0({32{1'b0}}), .in1(register_1_q), .in2(register_2_q), .in3(register_3_q), .in4(register_4_q),
    .in5(register_5_q), .in6(register_6_q), .in7(register_7_q), .in8(register_8_q), .in9(register_9_q),
    .in10(register_10_q), .in11(register_11_q), .in12(register_12_q), .in13(register_13_q),
    .in14(register_14_q), .in15(register_15_q), .out(Out2), .sel(RS2));
  Decoder #(.select(4)) decoder_1 (
    .out1(decoder_1_out1), .out2(decoder_1_out2), .out3(decoder_1_out3), .out4(decoder_1_out4),
    .out5(decoder_1_out5), .out6(decoder_1_out6), .out7(decoder_1_out7), .out8(decoder_1_out8),
    .out9(decoder_1_out9), .out10(decoder_1_out10), .out11(decoder_1_out11), .out12(decoder_1_out12),
    .out13(decoder_1_out13), .out14(decoder_1_out14), .out15(decoder_1_out15), .sel(RD), .en(Write));  // open: out0
  Register #(.trigger("falling"), .width(32)) register_1 (
    .D(Data), .en(decoder_1_out1), .clk(Clock), .Q(register_1_q));  // open: clr
  Register #(.trigger("falling"), .width(32)) register_2 (
    .D(Data), .en(decoder_1_out2), .clk(Clock), .Q(register_2_q));  // open: clr
  Register #(.trigger("falling"), .width(32)) register_3 (
    .D(Data), .en(decoder_1_out3), .clk(Clock), .Q(register_3_q));  // open: clr
  Register #(.trigger("falling"), .width(32)) register_4 (
    .D(Data), .en(decoder_1_out4), .clk(Clock), .Q(register_4_q));  // open: clr
  Register #(.trigger("falling"), .width(32)) register_5 (
    .D(Data), .en(decoder_1_out5), .clk(Clock), .Q(register_5_q));  // open: clr
  Register #(.trigger("falling"), .width(32)) register_6 (
    .D(Data), .en(decoder_1_out6), .clk(Clock), .Q(register_6_q));  // open: clr
  Register #(.trigger("falling"), .width(32)) register_7 (
    .D(Data), .en(decoder_1_out7), .clk(Clock), .Q(register_7_q));  // open: clr
  Register #(.trigger("falling"), .width(32)) register_8 (
    .D(Data), .en(decoder_1_out8), .clk(Clock), .Q(register_8_q));  // open: clr
  Register #(.trigger("falling"), .width(32)) register_9 (
    .D(Data), .en(decoder_1_out9), .clk(Clock), .Q(register_9_q));  // open: clr
  Register #(.trigger("falling"), .width(32)) register_10 (
    .D(Data), .en(decoder_1_out10), .clk(Clock), .Q(register_10_q));  // open: clr
  Register #(.trigger("falling"), .width(32)) register_11 (
    .D(Data), .en(decoder_1_out11), .clk(Clock), .Q(register_11_q));  // open: clr
  Register #(.trigger("falling"), .width(32)) register_12 (
    .D(Data), .en(decoder_1_out12), .clk(Clock), .Q(register_12_q));  // open: clr
  Register #(.trigger("falling"), .width(32)) register_13 (
    .D(Data), .en(decoder_1_out13), .clk(Clock), .Q(register_13_q));  // open: clr
  Register #(.trigger("falling"), .width(32)) register_14 (
    .D(Data), .en(decoder_1_out14), .clk(Clock), .Q(register_14_q));  // open: clr
  Register #(.trigger("falling"), .width(32)) register_15 (
    .D(Data), .en(decoder_1_out15), .clk(Clock), .Q(register_15_q));  // open: clr

  // Notes on the sheet:
  //   ZERO
  //   RA
  //   SP
  //   GP
  //   TP
  //   T0
  //   T1
  //   T2
  //   S0
  //   S1
  //   A0
  //   A1
  //   S2
  //   S3
  //   S4
  //   S5
endmodule

module RegisterFile (
  input  [31:0] Data,
  input  [4:0] RD,
  input  Write,
  input  Clock,
  input  [4:0] RS1,
  input  [4:0] RS2,
  output [31:0] Out1,
  output [31:0] Out2
);

  wire demultiplexer_1_out0, demultiplexer_1_out1;
  wire [31:0] BottomRegisters_out1, BottomRegisters_out2, TopRegisters_out1;

  Demultiplexer demultiplexer_1 (.out0(demultiplexer_1_out0), .out1(demultiplexer_1_out1), .in(Write), .sel(RD[4]));
  Registers16WithZero BottomRegisters (
    .Write(demultiplexer_1_out0), .RD(RD[3:0]), .Clock(Clock), .Data(Data), .RS1(RS1[3:0]), .RS2(RS2[3:0]),
    .Out1(BottomRegisters_out1), .Out2(BottomRegisters_out2));
  Registers16 TopRegisters (
    .Write(demultiplexer_1_out1), .RD(RD[3:0]), .Clock(Clock), .Data(Data), .RS1(RS1[3:0]), .RS2(RS2[3:0]),
    .Out1(TopRegisters_out1), .Out2(TopRegisters_out1));
  Multiplexer #(.width(32)) multiplexer_1 (
    .in0(BottomRegisters_out1), .in1(TopRegisters_out1), .out(Out1), .sel(RS1[4]));
  Multiplexer #(.width(32)) multiplexer_2 (
    .in0(BottomRegisters_out2), .in1(TopRegisters_out1), .out(Out2), .sel(RS2[4]));
endmodule

module CPU (
  input  [31:0] Instruction,
  input  [31:0] LoadValue,
  input  Clock,
  input  Reset,
  output Illegal,
  output [2:0] MemWidth,
  output Store,
  output Load,
  output [31:0] MemAddr,
  output [31:0] StoreValue,
  output [31:0] PC
);

  wire and_1_out, branchunit_1_branch, decoder_1_out1, decoder_1_out2, decoder_1_out3, decoder_1_out4,
       decoder_1_out5, decoder_1_out6, decoder_1_out7, decoder_1_out9, decoder_1_out10, decoder_1_out11,
       decoder_1_out12, decoder_1_out13, decoder_1_out14, decoder_1_out15, decoder_1_out16, decoder_1_out17,
       decoder_1_out18, decoder_1_out19, decoder_1_out20, decoder_1_out21, decoder_1_out22, decoder_1_out23,
       decoder_1_out24, decoder_1_out25, decoder_1_out26, decoder_1_out27, decoder_1_out28, decoder_1_out29,
       decoder_1_out30, decoder_1_out31, extractor_1_bit30, nand_1_out, or_2_out, or_5_out, or_6_out,
       or_7_out, priority_encoder_1_p2, priority_encoder_1_p6;
  wire [1:0] extractor_1_opcode;
  wire [2:0] priority_encoder_1_p5;
  wire [4:0] extractor_1_opcode_2, extractor_1_rd, extractor_1_rs1, extractor_1_rs2;
  wire [31:0] adder_1_out, adder_2_out, adder_3_out, adder_4_out, alu_1_data, controlled_buffer_1_out,
       extractor_1_immediate, multiplexer_1_out, multiplexer_2_out, registerfile_1_out1, registerfile_1_out2;

  Register #(.trigger("falling"), .width(32)) register_1 (
    .D(multiplexer_1_out), .clk(Clock), .Q(PC), .clr(Reset));  // open: en
  Decoder #(.select(5)) decoder_1 (
    .out0(Load), .out1(decoder_1_out1), .out2(decoder_1_out2), .out3(decoder_1_out3), .out4(decoder_1_out4),
    .out5(decoder_1_out5), .out6(decoder_1_out6), .out7(decoder_1_out7), .out8(Store), .out9(decoder_1_out9),
    .out10(decoder_1_out10), .out11(decoder_1_out11), .out12(decoder_1_out12), .out13(decoder_1_out13),
    .out14(decoder_1_out14), .out15(decoder_1_out15), .out16(decoder_1_out16), .out17(decoder_1_out17),
    .out18(decoder_1_out18), .out19(decoder_1_out19), .out20(decoder_1_out20), .out21(decoder_1_out21),
    .out22(decoder_1_out22), .out23(decoder_1_out23), .out24(decoder_1_out24), .out25(decoder_1_out25),
    .out26(decoder_1_out26), .out27(decoder_1_out27), .out28(decoder_1_out28), .out29(decoder_1_out29),
    .out30(decoder_1_out30), .out31(decoder_1_out31), .sel(extractor_1_opcode_2));  // open: en
  Extractor extractor_1 (
    .Instruction(Instruction), .Format(priority_encoder_1_p5),
    .Opcode({extractor_1_opcode_2, extractor_1_opcode}), .RD(extractor_1_rd), .Funct3(MemWidth),
    .RS1(extractor_1_rs1), .RS2(extractor_1_rs2), .Bit30(extractor_1_bit30), .Immediate(extractor_1_immediate));
  nand nand_1 (nand_1_out, extractor_1_opcode[1], extractor_1_opcode[0]);
  Multiplexer #(.width(32)) multiplexer_1 (
    .in0(adder_2_out), .in1(adder_4_out), .out(multiplexer_1_out), .sel(decoder_1_out25));
  or or_1 (Illegal, nand_1_out, decoder_1_out31, decoder_1_out30, decoder_1_out29, decoder_1_out26, decoder_1_out23, decoder_1_out22, decoder_1_out21, decoder_1_out20, decoder_1_out19, decoder_1_out18, decoder_1_out28, decoder_1_out17, decoder_1_out16, decoder_1_out15, decoder_1_out14, decoder_1_out11, decoder_1_out10, decoder_1_out9, decoder_1_out7, decoder_1_out6, decoder_1_out2, decoder_1_out1);
  assign controlled_buffer_1_out = decoder_1_out5 ? adder_1_out : 32'bz;  // Controlled_Buffer controlled_buffer_1
  Adder #(.width(32)) adder_1 (.a(PC), .b(extractor_1_immediate), .out(adder_1_out));  // open: cin, cout
  Multiplexer #(.width(32)) multiplexer_2 (
    .in0(32'h4), .in1(extractor_1_immediate), .out(multiplexer_2_out), .sel(or_5_out));
  Adder #(.width(32)) adder_2 (.a(PC), .b(multiplexer_2_out), .out(adder_2_out));  // open: cin, cout
  assign controlled_buffer_1_out = or_2_out ? adder_3_out : 32'bz;  // Controlled_Buffer controlled_buffer_2
  Adder #(.width(32)) adder_3 (.a(PC), .b(32'h4), .out(adder_3_out));  // open: cin, cout
  // Priority_Encoder priority_encoder_1: pin names not known; wires that end beside it: decoder_1_out12, priority_encoder_1_p2, Store, decoder_1_out24, priority_encoder_1_p5, priority_encoder_1_p6, decoder_1_out27, 1'b0, 1'b0
  RegisterFile registerfile_1 (
    .Data(controlled_buffer_1_out), .RD(extractor_1_rd), .Write(or_6_out), .Clock(Clock),
    .RS1(extractor_1_rs1), .RS2(extractor_1_rs2), .Out1(registerfile_1_out1), .Out2(registerfile_1_out2));
  Multiplexer #(.width(32)) multiplexer_3 (
    .in0(registerfile_1_out2), .in1(extractor_1_immediate), .out(StoreValue), .sel(decoder_1_out4));
  assign controlled_buffer_1_out = decoder_1_out13 ? extractor_1_immediate : 32'bz;  // Controlled_Buffer controlled_buffer_3
  or or_2 (or_2_out, decoder_1_out27, decoder_1_out25);
  or or_3 (priority_encoder_1_p6, decoder_1_out13, decoder_1_out5);
  or or_4 (priority_encoder_1_p2, decoder_1_out28, decoder_1_out3, decoder_1_out4, Load, decoder_1_out25);
  and and_1 (and_1_out, branchunit_1_branch, decoder_1_out24);
  or or_5 (or_5_out, and_1_out, decoder_1_out27);
  or or_6 (or_6_out, decoder_1_out25, decoder_1_out12, decoder_1_out4, Load, decoder_1_out5, decoder_1_out13, decoder_1_out27);
  Adder #(.width(32)) adder_4 (
    .a(registerfile_1_out1), .b(extractor_1_immediate), .out(adder_4_out));  // open: cin, cout
  or or_7 (or_7_out, decoder_1_out12, decoder_1_out4);
  ALU alu_1 (
    .A(registerfile_1_out1), .B(StoreValue), .Funct3(MemWidth), .Bit30(extractor_1_bit30),
    .Imm(decoder_1_out4), .Data(alu_1_data));
  assign controlled_buffer_1_out = or_7_out ? alu_1_data : 32'bz;  // Controlled_Buffer controlled_buffer_4
  BranchUnit branchunit_1 (.A(registerfile_1_out1), .B(StoreValue), .Funct3(MemWidth), .Branch(branchunit_1_branch));
  assign controlled_buffer_1_out = Load ? LoadValue : 32'bz;  // Controlled_Buffer controlled_buffer_5
  Adder #(.width(32)) adder_5 (.a(registerfile_1_out1), .b(extractor_1_immediate), .out(MemAddr));  // open: cin, cout

  // Notes on the sheet:
  //   AUIPC
  //   Relative Jump?
  //   Store PC?
  //   JALR
  //   A
  //   Imm
  //   B
endmodule

module ALU (
  input  [31:0] A,
  input  [31:0] B,
  input  [2:0] Funct3,
  input  Bit30,
  input  Imm,
  output [31:0] Data
);

  wire and_1_out, not_1_out;
  wire [0:0] comparator_1_lt, comparator_2_lt;
  wire [31:0] adder_1_out, and_2_out, multiplexer_1_out, multiplexer_2_out, or_1_out, shifter_1_out,
       shifter_2_out, shifter_3_out, subtractor_1_out, xor_1_out;

  and and_1 (and_1_out, Bit30, not_1_out);
  not not_1 (not_1_out, Imm);
  assign xor_1_out = A ^ B;  // XOR_Gate xor_1, 32 bits wide
  assign or_1_out = A | B;  // OR_Gate or_1, 32 bits wide
  assign and_2_out = A & B;  // AND_Gate and_2, 32 bits wide
  Shifter #(.width(32)) shifter_1 (.in(A), .\dist (B[4:0]), .out(shifter_1_out));
  Shifter #(.shift("lr"), .width(32)) shifter_2 (.in(A), .\dist (B[4:0]), .out(shifter_2_out));
  Multiplexer #(.width(32)) multiplexer_1 (
    .in0(shifter_2_out), .in1(shifter_3_out), .out(multiplexer_1_out), .sel(Bit30));
  Shifter #(.shift("ar"), .width(32)) shifter_3 (.in(A), .\dist (B[4:0]), .out(shifter_3_out));
  Adder #(.width(32)) adder_1 (.a(A), .b(B), .out(adder_1_out));  // open: cin, cout
  Multiplexer #(.width(32)) multiplexer_2 (
    .in0(adder_1_out), .in1(subtractor_1_out), .out(multiplexer_2_out), .sel(and_1_out));
  Subtractor #(.width(32)) subtractor_1 (.a(A), .b(B), .out(subtractor_1_out));  // open: bin, bout
  Comparator #(.width(32)) comparator_1 (.a(A), .b(B), .lt(comparator_1_lt[0]));  // open: gt, eq
  Comparator #(.mode("unsigned"), .width(32)) comparator_2 (.a(A), .b(B), .lt(comparator_2_lt[0]));  // open: gt, eq
  Multiplexer #(.select(3), .width(32)) multiplexer_3 (
    .in0(multiplexer_2_out), .in1({{31{1'b0}}, comparator_1_lt[0]}), .in2({{31{1'b0}}, comparator_2_lt[0]}),
    .in3(xor_1_out), .in4(or_1_out), .in5(and_2_out), .in6(shifter_1_out), .in7(multiplexer_1_out),
    .out(Data), .sel(Funct3));
endmodule

module BranchUnit (
  input  [31:0] A,
  input  [31:0] B,
  input  [2:0] Funct3,
  output Branch
);

  wire comparator_1_eq, comparator_1_gt, comparator_1_lt, comparator_2_eq, comparator_2_gt, comparator_2_lt,
       not_1_out, or_1_out, or_2_out;

  Comparator #(.width(32)) comparator_1 (
    .a(A), .b(B), .gt(comparator_1_gt), .eq(comparator_1_eq), .lt(comparator_1_lt));
  Comparator #(.mode("unsigned"), .width(32)) comparator_2 (
    .a(A), .b(B), .gt(comparator_2_gt), .eq(comparator_2_eq), .lt(comparator_2_lt));
  not not_1 (not_1_out, comparator_1_eq);
  or or_1 (or_1_out, comparator_1_gt, comparator_1_eq);
  or or_2 (or_2_out, comparator_2_gt, comparator_2_eq);
  Multiplexer #(.select(3)) multiplexer_1 (
    .in0(comparator_1_eq), .in1(not_1_out), .in2(comparator_1_lt), .in3(or_1_out), .in4(comparator_2_lt),
    .in5(or_2_out), .in6(1'b0), .in7(1'b0), .out(Branch), .sel(Funct3));
endmodule

module Memory (
  input  [31:0] Address,
  input  Store,
  input  Load,
  input  [2:0] Width,
  input  [31:0] StoreValue,
  input  Clock,
  output [31:0] LoadValue
);

  RAM #(.addrWidth(24), .asyncread("true"), .dataWidth(32), .trigger("falling")) ram_1 (
    .addr(Address[25:2]), .we(Store), .oe(Load), .clk(Clock), .din(StoreValue), .dout(LoadValue));
endmodule
